# Fritzing sketch cruceSemaforos (saved by Fritzing 0.9.2b)
breadboards: 1

parts:
  Parte1 = Arduino Uno (Rev3)
  LED1 = LED - 5mm [color="Yellow (595nm)" package="5 mm [THT]"]
  LED2 = LED - 5mm [color="Red (633nm)" package="5 mm [THT]"]
  LED3 = LED - 5mm [color="Green (555nm)" package="5 mm [THT]"]
  LED5 = LED - 5mm [color="Green (555nm)" package="5 mm [THT]"]
  LED6 = LED - 5mm [color="Yellow (595nm)" package="5 mm [THT]"]
  S1 = Pushbutton [package="[THT]"]
  S2 = Pushbutton [package="[THT]"]
  R1 = Resistor [tolerance=±5% resistance=470 package=THT]
  R2 = Resistor [tolerance=±5% resistance=470 package=THT]
  R3 = Resistor [tolerance=±5% resistance=470 package=THT]
  R4 = Resistor [tolerance=±5% resistance=470 package=THT]
  R6 = Resistor [tolerance=±5% resistance=10k package=THT]
  R7 = Resistor [tolerance=±5% resistance=470 package=THT]
  R8 = Resistor [tolerance=±5% resistance=470 package=THT]
  LED4 = LED - 5mm [color="Red (633nm)" package="5 mm [THT]"]
  R5 = Resistor [tolerance=±5% resistance=10k package=THT]

nets:
  N1: Parte1.D8, R2.Pin_0
  N2: Parte1.D9_PWM, S1.Pin_1, S1.Pin_2, R5.Pin_0
  N3: Parte1.D2, S2.Pin_1, S2.Pin_2, R6.Pin_0
  N4: Parte1.D3_PWM, R1.Pin_0
  N5: Parte1.D4, R4.Pin_0
  N6: Parte1.D5_PWM, R7.Pin_0
  N7: Parte1.D6_PWM, R8.Pin_0
  N8: Parte1.D7, R3.Pin_0
  N9: Parte1.5V, S1.Pin_3, S1.Pin_4, S2.Pin_3, S2.Pin_4
  N10: Parte1.GND, LED1.cathode, LED2.cathode, LED3.cathode, LED5.cathode, LED6.cathode, R6.Pin_1, LED4.cathode, R5.Pin_1
  N11: LED1.anode, R4.Pin_1
  N12: LED2.anode, R1.Pin_1
  N13: LED3.anode, R7.Pin_1
  N14: LED5.anode, R2.Pin_1
  N15: LED6.anode, R3.Pin_1
  N16: R8.Pin_1, LED4.anode
