# Fritzing sketch dado (saved by Fritzing 0.9.2b)
breadboards: 1

parts:
  Parte1 = Arduino Uno (Rev3)
  LED5 = LED - 5mm [color="Blue (430nm)" package="5 mm [THT]"]
  S1 = Pushbutton [package="[THT]"]
  R3 = Resistor [tolerance=±5% resistance=470 package=THT]
  R6 = Resistor [tolerance=±5% resistance=10k package=THT]
  LED8 = LED - 5mm [color="Blue (430nm)" package="5 mm [THT]"]
  LED9 = LED - 5mm [color="Blue (430nm)" package="5 mm [THT]"]
  LED10 = LED - 5mm [color="Blue (430nm)" package="5 mm [THT]"]
  LED11 = LED - 5mm [color="Blue (430nm)" package="5 mm [THT]"]
  LED12 = LED - 5mm [color="Blue (430nm)" package="5 mm [THT]"]
  LED13 = LED - 5mm [color="Blue (430nm)" package="5 mm [THT]"]
  R7 = Resistor [tolerance=±5% resistance=470 package=THT]
  R8 = Resistor [tolerance=±5% resistance=470 package=THT]
  R9 = Resistor [tolerance=±5% resistance=470 package=THT]
  R10 = Resistor [tolerance=±5% resistance=470 package=THT]
  R11 = Resistor [tolerance=±5% resistance=470 package=THT]
  R12 = Resistor [tolerance=±5% resistance=470 package=THT]

nets:
  N1: Parte1.D8, R12.Pin_0
  N2: Parte1.D9_PWM, S1.Pin_1, S1.Pin_2, R6.Pin_0
  N3: Parte1.D2, R3.Pin_0
  N4: Parte1.D3_PWM, R9.Pin_0
  N5: Parte1.D4, R8.Pin_0
  N6: Parte1.D5_PWM, R11.Pin_0
  N7: Parte1.D6_PWM, R10.Pin_0
  N8: Parte1.D7, R7.Pin_0
  N9: Parte1.5V, S1.Pin_3, S1.Pin_4
  N10: Parte1.GND, LED5.cathode, R6.Pin_1, LED8.cathode, LED9.cathode, LED10.cathode, LED11.cathode, LED12.cathode, LED13.cathode
  N11: LED5.anode, R11.Pin_1
  N12: R3.Pin_1, LED11.anode
  N13: LED8.anode, R10.Pin_1
  N14: LED9.anode, R8.Pin_1
  N15: LED10.anode, R9.Pin_1
  N16: LED12.anode, R12.Pin_1
  N17: LED13.anode, R7.Pin_1
