# Fritzing sketch reproductorMusica (saved by Fritzing 0.9.2b)
breadboards: 1

parts:
  Parte1 = Arduino Uno (Rev3)
  S1 = Pushbutton [package="[THT]"]
  R2 = Trimmer Potentiometer [maximum_resistance=10kΩ package=THT]
  J1 = Piezo Speaker
  R1 = Resistor [tolerance=±5% resistance=10k package="2512 [SMD]"]
  R1_2 = Resistor [tolerance=±5% resistance=10k package="2010 [SMD]"]
  R1_3 = Resistor [tolerance=±5% resistance=10k package=THT]

nets:
  N1: Parte1.D8, R2.leg1
  N2: Parte1.D2, S1.Pin_1, S1.Pin_2, R1.Pin_0, R1_2.Pin_0, R1_3.Pin_0
  N3: Parte1.5V, S1.Pin_3, S1.Pin_4
  N4: Parte1.GND, J1.pin1, R1.Pin_1, R1_2.Pin_1, R1_3.Pin_1
  N5: R2.wiper, J1.pin2
